# Fritzing sketch arduino-dehumidifier-sensor (saved by Fritzing 0.9.4)
breadboards: 1

parts:
  Part1 = Adafruit Feather HUZZAH ESP8266 [part_number="Adafruit #2821"]
  AM1 = AM2302 Humidity and Temperature Sensor
  Part2 = Adafruit GA1A1S202WP [part_number="Adafruit #1384"]

nets:
  N1: Part1.GPIO13/MOSI, AM1.DATA
  N2: Part1.ADC, Part2.OUT
  GND: Part1.GND, AM1.GND, Part2.GND
  3.3V: Part1.3.3V, AM1.VDD, Part2.VCC

custom parts:
  Adafruit Feather HUZZAH ESP8266: his is the Adafruit Feather HUZZAH ESP8266 - our take on an 'all-in-one' ESP8266 WiFi development board with built in USB and battery charging. Its an ESP8266 WiFi module with all the extras you need, ready to rock! We have other boards in the Feather family, check'em out here. At the Feather HUZZAH's heart is an ESP8266 WiFi microcontroller clocked at 80 MHz and at 3.3V logic. This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
  Adafruit GA1A1S202WP: Upgrade a project that uses a photocell with the GA1A12S202 analog light sensor. Like a CdS photo-cell, the sensor does not require a microcontroller, the analog voltage output increases with the amount of light shining on the sensor face. This sensor has a lot of improvements that make it better for nearly any project. The biggest improvement over plain photocells is a true log-lin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
